// Logisim project CPU.circ as structural Verilog: 16 circuits, main circuit main
module main (
  input  in_1
);

  wire button_1_out, button_2_out, CLK, clock_1_out, comparator_1_eq, is_hlt, manual_clk_out,
       multiplexer_1_out, or_1_out, sreg_1_o, sreg_1_we, start_stop_out, t_ff_1_q, wmem_1_we;
  wire [1:0] flags;
  wire [9:0] branch_1_o, DMA, PC;
  wire [15:0] DMEM, regs_1_o0, regs_1_o1, ULA;
  wire [15:10] INST;

  Comparator #(.mode("unsigned"), .width(6)) comparator_1 (
    .a({6{1'b1}}), .b(INST), .eq(comparator_1_eq));  // open: gt, lt
  ED ed_1 (.i(comparator_1_eq), .o(is_hlt));
  RAM #(.addrWidth(10), .dataWidth(16), .enables("line")) IMEM (.addr(PC), .dout({INST, DMA}));  // open: we, clk, din
  Clock clock_1 (.out(clock_1_out));
  Button manual_clk (.out(manual_clk_out));
  T_Flip_Flop t_ff_1 (.T(1'b1), .clk(start_stop_out), .Q(t_ff_1_q), .reset(is_hlt));  // open: Qn, preset
  Button start_stop (.out(start_stop_out));
  Multiplexer multiplexer_1 (.in0(clock_1_out), .in1(manual_clk_out), .out(multiplexer_1_out), .sel(in_1));
  and and_1 (CLK, multiplexer_1_out, t_ff_1_q);
  BRANCH branch_1 (.INST({INST, DMA}), .SZ(flags), .PC(PC), .o(branch_1_o));
  REGS regs_1 (
    .sreg(sreg_1_o), .clk(CLK), .we(sreg_1_we), .in_3(button_1_out), .i(ULA), .o0(regs_1_o0), .o1(regs_1_o1));
  SREG sreg_1 (.op(INST), .a0(DMA[0]), .we(sreg_1_we), .o(sreg_1_o));
  Button button_1 (.out(button_1_out));
  Register #(.width(10)) register_1 (.D(branch_1_o), .en(1'b1), .clk(CLK), .Q(PC), .clr(or_1_out));
  or or_1 (or_1_out, button_2_out, is_hlt);
  Button button_2 (.out(button_2_out));
  display_dec16 a (.i(regs_1_o0));
  display_dec16 b (.i(regs_1_o1));
  SZ sz_1 (.i(ULA), .we(sreg_1_we), .clk(CLK), .R(button_1_out), .s(flags[1]), .z(flags[0]));
  ALU alu_1 (.a(regs_1_o0), .b(regs_1_o1), .mem(DMEM), .op(INST), .im(DMA), .o(ULA));
  WMEM wmem_1 (.op(INST), .we(wmem_1_we));
  RAM #(.addrWidth(10), .dataWidth(16), .enables("line")) u_DMEM (
    .addr(DMA), .we(wmem_1_we), .clk(CLK), .din(ULA), .dout(DMEM));
  display_dec16 u_inst (.i({INST, DMA}));

  // Other names for the same wires on the sheet: INST[9:0] = DMA; OP[5:0] = INST
endmodule

module REGS (
  input  sreg,
  input  clk,
  input  in_3,
  input  [15:0] i,
  input  we,
  output [15:0] o0,
  output [15:0] o1
);

  wire decoder_1_out0, decoder_1_out1;

  Decoder decoder_1 (.out0(decoder_1_out0), .out1(decoder_1_out1), .sel(sreg), .en(we));
  Register #(.width(16)) A (.D(i), .en(decoder_1_out0), .clk(clk), .Q(o0), .clr(in_3));
  Register #(.width(16)) B (.D(i), .en(decoder_1_out1), .clk(clk), .Q(o1), .clr(in_3));
endmodule

module buff1b (
  input  in_1,
  input  in_2,
  output out_3
);

  and and_1 (out_3, in_1, in_2);
endmodule

module buff16b (
  input  [15:0] i,
  input  ctrl,
  output [15:0] o
);

  buff1b buff1b_1 (.in_1(i[0]), .in_2(ctrl), .out_3(o[0]));
  buff1b buff1b_2 (.in_1(i[1]), .in_2(ctrl), .out_3(o[1]));
  buff1b buff1b_3 (.in_1(i[2]), .in_2(ctrl), .out_3(o[2]));
  buff1b buff1b_4 (.in_1(i[3]), .in_2(ctrl), .out_3(o[3]));
  buff1b buff1b_5 (.in_1(i[4]), .in_2(ctrl), .out_3(o[4]));
  buff1b buff1b_6 (.in_1(i[5]), .in_2(ctrl), .out_3(o[5]));
  buff1b buff1b_7 (.in_1(i[6]), .in_2(ctrl), .out_3(o[6]));
  buff1b buff1b_8 (.in_1(i[7]), .in_2(ctrl), .out_3(o[7]));
  buff1b buff1b_9 (.in_1(i[8]), .in_2(ctrl), .out_3(o[8]));
  buff1b buff1b_10 (.in_1(i[9]), .in_2(ctrl), .out_3(o[9]));
  buff1b buff1b_11 (.in_1(i[10]), .in_2(ctrl), .out_3(o[10]));
  buff1b buff1b_12 (.in_1(i[11]), .in_2(ctrl), .out_3(o[11]));
  buff1b buff1b_13 (.in_1(i[12]), .in_2(ctrl), .out_3(o[12]));
  buff1b buff1b_14 (.in_1(i[13]), .in_2(ctrl), .out_3(o[13]));
  buff1b buff1b_15 (.in_1(i[14]), .in_2(ctrl), .out_3(o[14]));
  buff1b buff1b_16 (.in_1(i[15]), .in_2(ctrl), .out_3(o[15]));
endmodule

module ALU (
  input  [5:0] op,
  input  [15:0] a,
  input  [15:0] b,
  input  [15:0] mem,
  input  [9:0] im,
  output [15:0] o
);

  wire decoder_1_out1, decoder_1_out2, decoder_1_out3, decoder_1_out4, decoder_1_out5, decoder_1_out6,
       decoder_1_out7, decoder_1_out8, decoder_1_out9, decoder_1_out10, decoder_1_out11, decoder_1_out12,
       decoder_1_out13, decoder_1_out14, decoder_1_out15, decoder_1_out16, decoder_1_out17, decoder_1_out18,
       decoder_1_out19, decoder_1_out20, decoder_1_out21, decoder_1_out22, decoder_1_out23, not_1_out,
       or_4_out, or_5_out;
  wire [15:0] adder_1_out, adder_2_out, adder_3_out, and_1_out, and_2_out, and_3_out, bit_extender_1_out,
       buff16b_1_o, buff16b_2_o, buff16b_3_o, buff16b_4_o, buff16b_5_o, buff16b_6_o, buff16b_7_o,
       buff16b_8_o, buff16b_9_o, buff16b_10_o, buff16b_11_o, buff16b_12_o, buff16b_13_o, buff16b_14_o,
       buff16b_15_o, buff16b_16_o, buff16b_17_o, buff16b_18_o, buff16b_19_o, buff16b_20_o, buff16b_21_o,
       or_1_out, or_2_out, or_3_out, subtractor_1_out, subtractor_2_out, subtractor_3_out, xor_1_out,
       xor_2_out, xor_3_out;

  assign bit_extender_1_out = {{6{im[9]}}, im};  // Bit_Extender bit_extender_1
  Adder #(.width(16)) adder_1 (.a(a), .b(mem), .out(adder_1_out));  // open: cin, cout
  Subtractor #(.width(16)) subtractor_1 (.a(a), .b(b), .out(subtractor_1_out));  // open: bin, bout
  Subtractor #(.width(16)) subtractor_2 (.a(b), .b(mem), .out(subtractor_2_out));  // open: bin, bout
  assign and_1_out = a & b;  // AND_Gate and_1, 16 bits wide
  assign and_2_out = a & mem;  // AND_Gate and_2, 16 bits wide
  assign and_3_out = b & mem;  // AND_Gate and_3, 16 bits wide
  assign or_1_out = a | b;  // OR_Gate or_1, 16 bits wide
  assign or_2_out = a | mem;  // OR_Gate or_2, 16 bits wide
  assign or_3_out = b | mem;  // OR_Gate or_3, 16 bits wide
  assign xor_1_out = a ^ b;  // XOR_Gate xor_1, 16 bits wide
  assign xor_2_out = a ^ mem;  // XOR_Gate xor_2, 16 bits wide
  assign xor_3_out = b ^ mem;  // XOR_Gate xor_3, 16 bits wide
  Adder #(.width(16)) adder_2 (.a(a), .b(b), .out(adder_2_out));  // open: cin, cout
  Adder #(.width(16)) adder_3 (.a(b), .b(mem), .out(adder_3_out));  // open: cin, cout
  Subtractor #(.width(16)) subtractor_3 (.a(a), .b(mem), .out(subtractor_3_out));  // open: bin, bout
  not not_1 (not_1_out, op[5]);
  Decoder #(.select(5)) decoder_1 (
    .out1(decoder_1_out1), .out2(decoder_1_out2), .out3(decoder_1_out3), .out4(decoder_1_out4),
    .out5(decoder_1_out5), .out6(decoder_1_out6), .out7(decoder_1_out7), .out8(decoder_1_out8),
    .out9(decoder_1_out9), .out10(decoder_1_out10), .out11(decoder_1_out11), .out12(decoder_1_out12),
    .out13(decoder_1_out13), .out14(decoder_1_out14), .out15(decoder_1_out15), .out16(decoder_1_out16),
    .out17(decoder_1_out17), .out18(decoder_1_out18), .out19(decoder_1_out19), .out20(decoder_1_out20),
    .out21(decoder_1_out21), .out22(decoder_1_out22), .out23(decoder_1_out23), .sel(op[4:0]), .en(not_1_out));  // open: out0, out24, out25, out26, out27, out28, out29, out30, out31
  or or_4 (or_4_out, decoder_1_out4, decoder_1_out3);
  or or_5 (or_5_out, decoder_1_out6, decoder_1_out5);
  buff16b buff16b_1 (.i(a), .ctrl(decoder_1_out1), .o(buff16b_1_o));
  buff16b buff16b_2 (.i(b), .ctrl(decoder_1_out2), .o(buff16b_2_o));
  buff16b buff16b_3 (.i(mem), .ctrl(or_4_out), .o(buff16b_3_o));
  buff16b buff16b_4 (.i(bit_extender_1_out), .ctrl(or_5_out), .o(buff16b_4_o));
  buff16b buff16b_5 (.i(b), .ctrl(decoder_1_out7), .o(buff16b_5_o));
  buff16b buff16b_6 (.i(a), .ctrl(decoder_1_out8), .o(buff16b_6_o));
  buff16b buff16b_7 (.i(adder_2_out), .ctrl(decoder_1_out9), .o(buff16b_7_o));
  buff16b buff16b_8 (.i(adder_1_out), .ctrl(decoder_1_out10), .o(buff16b_8_o));
  buff16b buff16b_9 (.i(adder_3_out), .ctrl(decoder_1_out11), .o(buff16b_9_o));
  buff16b buff16b_10 (.i(subtractor_1_out), .ctrl(decoder_1_out12), .o(buff16b_10_o));
  buff16b buff16b_11 (.i(subtractor_3_out), .ctrl(decoder_1_out13), .o(buff16b_11_o));
  buff16b buff16b_12 (.i(subtractor_2_out), .ctrl(decoder_1_out14), .o(buff16b_12_o));
  buff16b buff16b_13 (.i(and_1_out), .ctrl(decoder_1_out15), .o(buff16b_13_o));
  buff16b buff16b_14 (.i(and_2_out), .ctrl(decoder_1_out16), .o(buff16b_14_o));
  buff16b buff16b_15 (.i(and_3_out), .ctrl(decoder_1_out17), .o(buff16b_15_o));
  buff16b buff16b_16 (.i(or_1_out), .ctrl(decoder_1_out18), .o(buff16b_16_o));
  buff16b buff16b_17 (.i(or_2_out), .ctrl(decoder_1_out19), .o(buff16b_17_o));
  buff16b buff16b_18 (.i(or_3_out), .ctrl(decoder_1_out20), .o(buff16b_18_o));
  buff16b buff16b_19 (.i(xor_1_out), .ctrl(decoder_1_out21), .o(buff16b_19_o));
  buff16b buff16b_20 (.i(xor_2_out), .ctrl(decoder_1_out22), .o(buff16b_20_o));
  buff16b buff16b_21 (.i(xor_3_out), .ctrl(decoder_1_out23), .o(buff16b_21_o));
  assign o = buff16b_1_o | buff16b_2_o | buff16b_3_o | buff16b_4_o | buff16b_5_o | buff16b_6_o | buff16b_7_o | buff16b_8_o | buff16b_9_o | buff16b_10_o | buff16b_11_o | buff16b_12_o | buff16b_13_o | buff16b_14_o | buff16b_15_o | buff16b_16_o | buff16b_17_o | buff16b_18_o | buff16b_19_o | buff16b_20_o | buff16b_21_o;  // OR_Gate or_6, 16 bits wide

  // Notes on the sheet:
  //   im: pull=down
endmodule

module SREG (
  input  [5:0] op,
  input  a0,
  output o,
  output we
);

  wire decoder_1_out3, decoder_1_out4, decoder_1_out5, decoder_1_out6, decoder_1_out7, decoder_1_out8,
       decoder_1_out9, decoder_1_out10, decoder_1_out11, decoder_1_out12, decoder_1_out13, decoder_1_out14,
       decoder_1_out15, decoder_1_out16, decoder_1_out17, decoder_1_out18, decoder_1_out19, decoder_1_out20,
       decoder_1_out21, decoder_1_out22, decoder_1_out23, not_1_out, or_1_out, or_2_out, or_4_out, or_5_out;

  not not_1 (not_1_out, op[5]);
  Decoder #(.select(5)) decoder_1 (
    .out3(decoder_1_out3), .out4(decoder_1_out4), .out5(decoder_1_out5), .out6(decoder_1_out6),
    .out7(decoder_1_out7), .out8(decoder_1_out8), .out9(decoder_1_out9), .out10(decoder_1_out10),
    .out11(decoder_1_out11), .out12(decoder_1_out12), .out13(decoder_1_out13), .out14(decoder_1_out14),
    .out15(decoder_1_out15), .out16(decoder_1_out16), .out17(decoder_1_out17), .out18(decoder_1_out18),
    .out19(decoder_1_out19), .out20(decoder_1_out20), .out21(decoder_1_out21), .out22(decoder_1_out22),
    .out23(decoder_1_out23), .sel(op[4:0]), .en(not_1_out));  // open: out0, out1, out2, out24, out25, out26, out27, out28, out29, out30, out31
  or or_1 (or_1_out, decoder_1_out3, decoder_1_out4, decoder_1_out5, decoder_1_out6, decoder_1_out7, decoder_1_out8, decoder_1_out9, decoder_1_out10, decoder_1_out11, decoder_1_out12, decoder_1_out13, decoder_1_out14, decoder_1_out15);
  or or_2 (or_2_out, decoder_1_out17, decoder_1_out18, decoder_1_out19, decoder_1_out20, decoder_1_out21, decoder_1_out22, decoder_1_out23);
  or or_3 (we, or_1_out, decoder_1_out16, or_2_out);
  or or_4 (or_4_out, decoder_1_out8, decoder_1_out23, decoder_1_out20, decoder_1_out17, decoder_1_out6, decoder_1_out14, decoder_1_out11, decoder_1_out4);
  or or_5 (or_5_out, decoder_1_out21, decoder_1_out18, decoder_1_out15, decoder_1_out12, decoder_1_out9);
  Decoder #(.select(5)) decoder_2 (
    .sel(op[4:0]), .en(op[5]));  // open: out0, out1, out2, out3, out4, out5, out6, out7, out8, out9, out10, out11, out12, out13, out14, out15, out16, out17, out18, out19, out20, out21, out22, out23, out24, out25, out26, out27, out28, out29, out30, out31
  Multiplexer multiplexer_1 (.in0(or_4_out), .in1(a0), .out(o), .sel(or_5_out));
endmodule

module WMEM (
  input  [5:0] op,
  output we
);

  wire comparator_1_eq, comparator_2_eq;

  Comparator #(.mode("unsigned"), .width(6)) comparator_1 (
    .a(op), .b(6'b000001), .eq(comparator_1_eq));  // open: gt, lt
  Comparator #(.mode("unsigned"), .width(6)) comparator_2 (
    .a(op), .b(6'b000010), .eq(comparator_2_eq));  // open: gt, lt
  or or_1 (we, comparator_1_eq, comparator_2_eq);
endmodule

module ED (
  input  i,
  output o
);

  wire not_1_out;

  not not_1 (not_1_out, i);
  and and_1 (o, not_1_out, i);
endmodule

module SZ (
  input  [15:0] i,
  input  we,
  input  clk,
  input  R,
  output s,
  output z
);

  wire nor_1_out;

  Register #(.width(1)) register_1 (.D(i[15]), .en(we), .clk(clk), .Q(s), .clr(R));
  Register #(.width(1)) register_2 (.D(nor_1_out), .en(we), .clk(clk), .Q(z), .clr(R));
  nor nor_1 (nor_1_out, i[15], i[14], i[13], i[12], i[11], i[10], i[9], i[8], i[7], i[6], i[5], i[4], i[3], i[2], i[1], i[0]);
endmodule

module BRANCH (
  input  [9:0] PC,
  input  [15:0] INST,
  input  [1:0] SZ,
  output [9:0] o
);

  wire and_1_out, and_2_out, comparator_1_eq, comparator_2_eq, comparator_3_eq, or_1_out;
  wire [9:0] adder_1_out;

  Comparator #(.mode("unsigned"), .width(6)) comparator_1 (
    .a(6'b011000), .b(INST[15:10]), .eq(comparator_1_eq));  // open: gt, lt
  Comparator #(.mode("unsigned"), .width(6)) comparator_2 (
    .a(6'b011001), .b(INST[15:10]), .eq(comparator_2_eq));  // open: gt, lt
  Comparator #(.mode("unsigned"), .width(6)) comparator_3 (
    .a(6'b011010), .b(INST[15:10]), .eq(comparator_3_eq));  // open: gt, lt
  or or_1 (or_1_out, comparator_1_eq, and_1_out, and_2_out);
  and and_1 (and_1_out, comparator_2_eq, SZ[1]);
  and and_2 (and_2_out, comparator_3_eq, SZ[0]);
  Adder #(.width(10)) adder_1 (.a(PC), .b(10'h1), .out(adder_1_out));  // open: cin, cout
  Multiplexer #(.width(10)) multiplexer_1 (.in0(adder_1_out), .in1(INST[9:0]), .out(o), .sel(or_1_out));
endmodule

module add3 (
  input  i3,
  input  i2,
  input  i1,
  input  i0,
  output o0,
  output o1,
  output o2,
  output o3
);

  wire and_1_out, and_2_out, and_3_out, and_4_out, and_5_out, and_6_out, and_7_out, and_8_out, and_9_out,
       and_10_out;

  and and_1 (and_1_out, i3, ~i0);  // AND_Gate
  and and_2 (and_2_out, ~i3, ~i2, i0);  // AND_Gate
  and and_3 (and_3_out, i2, i1, ~i0);  // AND_Gate
  and and_4 (and_4_out, i1, i0);
  and and_5 (and_5_out, i3, ~i0);  // AND_Gate
  and and_6 (and_6_out, ~i2, i1);  // AND_Gate
  and and_7 (and_7_out, i3, i0);
  and and_8 (and_8_out, i2, ~i1, ~i0);  // AND_Gate
  and and_9 (and_9_out, i2, i0);
  and and_10 (and_10_out, i2, i1);
  or or_1 (o0, and_1_out, and_2_out, and_3_out);
  or or_2 (o1, and_4_out, and_5_out, and_6_out);
  or or_3 (o2, and_7_out, and_8_out);
  or or_4 (o3, i3, and_9_out, and_10_out);
endmodule

module display_dec16 (
  input  [15:0] i
);

  wire add3_1_o0, add3_1_o1, add3_1_o2, add3_1_o3, add3_2_o0, add3_2_o1, add3_2_o2, add3_2_o3, add3_3_o0,
       add3_3_o1, add3_3_o2, add3_3_o3, add3_4_o0, add3_4_o1, add3_4_o2, add3_4_o3, add3_5_o0, add3_5_o1,
       add3_5_o2, add3_5_o3, add3_6_o0, add3_6_o1, add3_6_o2, add3_6_o3, add3_7_o0, add3_7_o1, add3_7_o2,
       add3_7_o3, add3_8_o0, add3_8_o1, add3_8_o2, add3_8_o3, add3_9_o0, add3_9_o1, add3_9_o2, add3_9_o3,
       add3_10_o0, add3_10_o1, add3_10_o2, add3_10_o3, add3_11_o0, add3_11_o1, add3_11_o2, add3_11_o3,
       add3_12_o0, add3_12_o1, add3_12_o2, add3_12_o3, add3_13_o0, add3_13_o1, add3_13_o2, add3_14_o0,
       add3_14_o1, add3_14_o2, add3_14_o3, add3_15_o0, add3_15_o1, add3_15_o2, add3_16_o0, add3_16_o1,
       add3_16_o2, add3_16_o3, add3_17_o0, add3_17_o1, add3_17_o2, add3_18_o0, add3_18_o1, add3_18_o2,
       add3_18_o3, add3_20_o0, add3_20_o1, add3_20_o2, add3_20_o3, add3_21_o0, add3_21_o1, add3_21_o2,
       add3_21_o3, add3_22_o0, add3_22_o1, add3_22_o2, add3_22_o3, add3_23_o0, add3_23_o1, add3_23_o2,
       add3_23_o3, add3_24_o0, add3_24_o1, add3_24_o2, add3_24_o3, add3_25_o0, add3_25_o1, add3_25_o2,
       add3_25_o3, add3_26_o0, add3_26_o1, add3_26_o2, add3_26_o3, add3_27_o0, add3_27_o1, add3_27_o2,
       add3_27_o3, add3_28_o0, add3_28_o1, add3_28_o2, add3_28_o3, add3_29_o0, add3_29_o1, add3_29_o2,
       add3_29_o3, add3_30_o0, add3_30_o1, add3_30_o2, add3_30_o3, add3_31_o0, add3_31_o1, add3_31_o2,
       add3_31_o3;
  wire [3:0] add3_19_o3, add3_32_o3, add3_33_o3, add3_34_o3;
  wire [3:1] add3_34_o0;

  Hex_Digit_Display d4 (.value(add3_19_o3));  // open: dp
  add3 add3_1 (
    .i3(1'b0), .i2(i[15]), .i1(i[14]), .i0(i[13]), .o0(add3_1_o0), .o1(add3_1_o1), .o2(add3_1_o2),
    .o3(add3_1_o3));
  add3 add3_2 (
    .i3(add3_1_o2), .i2(add3_1_o1), .i1(add3_1_o0), .i0(i[12]), .o0(add3_2_o0), .o1(add3_2_o1),
    .o2(add3_2_o2), .o3(add3_2_o3));
  add3 add3_3 (
    .i3(add3_2_o2), .i2(add3_2_o1), .i1(add3_2_o0), .i0(i[11]), .o0(add3_3_o0), .o1(add3_3_o1),
    .o2(add3_3_o2), .o3(add3_3_o3));
  add3 add3_4 (
    .i3(1'b0), .i2(add3_1_o3), .i1(add3_2_o3), .i0(add3_3_o3), .o0(add3_4_o0), .o1(add3_4_o1),
    .o2(add3_4_o2), .o3(add3_4_o3));
  add3 add3_5 (
    .i3(add3_3_o2), .i2(add3_3_o1), .i1(add3_3_o0), .i0(i[10]), .o0(add3_5_o0), .o1(add3_5_o1),
    .o2(add3_5_o2), .o3(add3_5_o3));
  add3 add3_6 (
    .i3(add3_4_o2), .i2(add3_4_o1), .i1(add3_4_o0), .i0(add3_5_o3), .o0(add3_6_o0), .o1(add3_6_o1),
    .o2(add3_6_o2), .o3(add3_6_o3));
  add3 add3_7 (
    .i3(add3_6_o2), .i2(add3_6_o1), .i1(add3_6_o0), .i0(add3_20_o3), .o0(add3_7_o0), .o1(add3_7_o1),
    .o2(add3_7_o2), .o3(add3_7_o3));
  add3 add3_8 (
    .i3(1'b0), .i2(add3_4_o3), .i1(add3_6_o3), .i0(add3_7_o3), .o0(add3_8_o0), .o1(add3_8_o1),
    .o2(add3_8_o2), .o3(add3_8_o3));
  add3 add3_9 (
    .i3(add3_7_o2), .i2(add3_7_o1), .i1(add3_7_o0), .i0(add3_21_o3), .o0(add3_9_o0), .o1(add3_9_o1),
    .o2(add3_9_o2), .o3(add3_9_o3));
  add3 add3_10 (
    .i3(add3_8_o2), .i2(add3_8_o1), .i1(add3_8_o0), .i0(add3_9_o3), .o0(add3_10_o0), .o1(add3_10_o1),
    .o2(add3_10_o2), .o3(add3_10_o3));
  add3 add3_11 (
    .i3(add3_9_o2), .i2(add3_9_o1), .i1(add3_9_o0), .i0(add3_22_o3), .o0(add3_11_o0), .o1(add3_11_o1),
    .o2(add3_11_o2), .o3(add3_11_o3));
  add3 add3_12 (
    .i3(add3_10_o2), .i2(add3_10_o1), .i1(add3_10_o0), .i0(add3_11_o3), .o0(add3_12_o0), .o1(add3_12_o1),
    .o2(add3_12_o2), .o3(add3_12_o3));
  add3 add3_13 (
    .i3(1'b0), .i2(add3_8_o3), .i1(add3_10_o3), .i0(add3_12_o3), .o0(add3_13_o0), .o1(add3_13_o1),
    .o2(add3_13_o2), .o3(add3_19_o3[3]));
  add3 add3_14 (
    .i3(add3_12_o2), .i2(add3_12_o1), .i1(add3_12_o0), .i0(add3_24_o3), .o0(add3_14_o0), .o1(add3_14_o1),
    .o2(add3_14_o2), .o3(add3_14_o3));
  add3 add3_15 (
    .i3(add3_13_o2), .i2(add3_13_o1), .i1(add3_13_o0), .i0(add3_14_o3), .o0(add3_15_o0), .o1(add3_15_o1),
    .o2(add3_15_o2), .o3(add3_19_o3[2]));
  add3 add3_16 (
    .i3(add3_14_o2), .i2(add3_14_o1), .i1(add3_14_o0), .i0(add3_26_o3), .o0(add3_16_o0), .o1(add3_16_o1),
    .o2(add3_16_o2), .o3(add3_16_o3));
  add3 add3_17 (
    .i3(add3_15_o2), .i2(add3_15_o1), .i1(add3_15_o0), .i0(add3_16_o3), .o0(add3_17_o0), .o1(add3_17_o1),
    .o2(add3_17_o2), .o3(add3_19_o3[1]));
  add3 add3_18 (
    .i3(add3_16_o2), .i2(add3_16_o1), .i1(add3_16_o0), .i0(add3_28_o3), .o0(add3_18_o0), .o1(add3_18_o1),
    .o2(add3_18_o2), .o3(add3_18_o3));
  add3 add3_19 (
    .i3(add3_17_o2), .i2(add3_17_o1), .i1(add3_17_o0), .i0(add3_18_o3), .o0(add3_32_o3[1]),
    .o1(add3_32_o3[2]), .o2(add3_32_o3[3]), .o3(add3_19_o3[0]));
  Hex_Digit_Display d3 (.value(add3_32_o3));  // open: dp
  add3 add3_20 (
    .i3(add3_5_o2), .i2(add3_5_o1), .i1(add3_5_o0), .i0(i[9]), .o0(add3_20_o0), .o1(add3_20_o1),
    .o2(add3_20_o2), .o3(add3_20_o3));
  add3 add3_21 (
    .i3(add3_20_o2), .i2(add3_20_o1), .i1(add3_20_o0), .i0(i[8]), .o0(add3_21_o0), .o1(add3_21_o1),
    .o2(add3_21_o2), .o3(add3_21_o3));
  add3 add3_22 (
    .i3(add3_21_o2), .i2(add3_21_o1), .i1(add3_21_o0), .i0(i[7]), .o0(add3_22_o0), .o1(add3_22_o1),
    .o2(add3_22_o2), .o3(add3_22_o3));
  add3 add3_23 (
    .i3(add3_22_o2), .i2(add3_22_o1), .i1(add3_22_o0), .i0(i[6]), .o0(add3_23_o0), .o1(add3_23_o1),
    .o2(add3_23_o2), .o3(add3_23_o3));
  add3 add3_24 (
    .i3(add3_11_o2), .i2(add3_11_o1), .i1(add3_11_o0), .i0(add3_23_o3), .o0(add3_24_o0), .o1(add3_24_o1),
    .o2(add3_24_o2), .o3(add3_24_o3));
  add3 add3_25 (
    .i3(add3_23_o2), .i2(add3_23_o1), .i1(add3_23_o0), .i0(i[5]), .o0(add3_25_o0), .o1(add3_25_o1),
    .o2(add3_25_o2), .o3(add3_25_o3));
  add3 add3_26 (
    .i3(add3_24_o2), .i2(add3_24_o1), .i1(add3_24_o0), .i0(add3_25_o3), .o0(add3_26_o0), .o1(add3_26_o1),
    .o2(add3_26_o2), .o3(add3_26_o3));
  add3 add3_27 (
    .i3(add3_25_o2), .i2(add3_25_o1), .i1(add3_25_o0), .i0(i[4]), .o0(add3_27_o0), .o1(add3_27_o1),
    .o2(add3_27_o2), .o3(add3_27_o3));
  add3 add3_28 (
    .i3(add3_26_o2), .i2(add3_26_o1), .i1(add3_26_o0), .i0(add3_27_o3), .o0(add3_28_o0), .o1(add3_28_o1),
    .o2(add3_28_o2), .o3(add3_28_o3));
  add3 add3_29 (
    .i3(add3_27_o2), .i2(add3_27_o1), .i1(add3_27_o0), .i0(i[3]), .o0(add3_29_o0), .o1(add3_29_o1),
    .o2(add3_29_o2), .o3(add3_29_o3));
  add3 add3_30 (
    .i3(add3_28_o2), .i2(add3_28_o1), .i1(add3_28_o0), .i0(add3_29_o3), .o0(add3_30_o0), .o1(add3_30_o1),
    .o2(add3_30_o2), .o3(add3_30_o3));
  add3 add3_31 (
    .i3(add3_29_o2), .i2(add3_29_o1), .i1(add3_29_o0), .i0(i[2]), .o0(add3_31_o0), .o1(add3_31_o1),
    .o2(add3_31_o2), .o3(add3_31_o3));
  add3 add3_32 (
    .i3(add3_18_o2), .i2(add3_18_o1), .i1(add3_18_o0), .i0(add3_30_o3), .o0(add3_33_o3[1]),
    .o1(add3_33_o3[2]), .o2(add3_33_o3[3]), .o3(add3_32_o3[0]));
  add3 add3_33 (
    .i3(add3_30_o2), .i2(add3_30_o1), .i1(add3_30_o0), .i0(add3_31_o3), .o0(add3_34_o3[1]),
    .o1(add3_34_o3[2]), .o2(add3_34_o3[3]), .o3(add3_33_o3[0]));
  Hex_Digit_Display d2 (.value(add3_33_o3));  // open: dp
  Hex_Digit_Display d1 (.value(add3_34_o3));  // open: dp
  add3 add3_34 (
    .i3(add3_31_o2), .i2(add3_31_o1), .i1(add3_31_o0), .i0(i[1]), .o0(add3_34_o0[1]), .o1(add3_34_o0[2]),
    .o2(add3_34_o0[3]), .o3(add3_34_o3[0]));
  Hex_Digit_Display d0 (.value({add3_34_o0, i[0]}));  // open: dp
endmodule

module shl (
  input  [7:0] i,
  output [7:0] o,
  output cout
);


  assign cout = i[7];
  assign o = {i[6:0], 1'b0};
endmodule

module shr (
  input  [7:0] i,
  output [7:0] o,
  output cout
);


  assign cout = i[0];
  assign o = {1'b0, i[7:1]};
endmodule

module roll_left (
  input  [7:0] i,
  input  cin,
  output [7:0] o,
  output cout
);


  assign cout = i[7];
  assign o = {i[6:0], cin};
endmodule

module roll_right (
  input  [7:0] i,
  input  cin,
  output [7:0] o,
  output cout
);


  assign cout = i[0];
  assign o = {cin, i[7:1]};
endmodule
